# Fritzing sketch FitoutSchematic (saved by Fritzing 0.9.2b)
breadboards: 1

parts:
  X1 = RELAY-2 [package=relay-g5v]
  D1 = Diode [package=diode-hv]
  Q1 = NPN-Transistor [package="TO92 [THT]"]
  R1 = Resistor [tolerance=±5% resistance=1k package="0805 [SMD]"]
  R2 = Resistor [tolerance=±5% resistance=10k package="0805 [SMD]"]
  X2 = RELAY-2 [package=relay-g5v]
  D2 = Diode [package=diode-hv]
  Q2 = NPN-Transistor [package="TO92 [THT]"]
  R3 = Resistor [tolerance=±5% resistance=1k package="0805 [SMD]"]
  R4 = Resistor [tolerance=±5% resistance=10k package="0805 [SMD]"]
  X3 = RELAY-2 [package=relay-g5v]
  D3 = Diode [package=diode-hv]
  Q3 = NPN-Transistor [package="TO92 [THT]"]
  R5 = Resistor [tolerance=±5% resistance=1k package="0805 [SMD]"]
  R6 = Resistor [tolerance=±5% resistance=10k package="0805 [SMD]"]
  S1 = Round Pushbutton
  S2 = Round Pushbutton
  S3 = Round Pushbutton
  X4 = RELAY-2 [package=relay-g5v]
  S5 = Round Pushbutton
  R7 = Resistor [tolerance=±5% resistance=10k package="0805 [SMD]"]
  R8 = Resistor [tolerance=±5% resistance=10k package="0805 [SMD]"]
  R9 = Resistor [tolerance=±5% resistance=10k package="0805 [SMD]"]
  R10 = Resistor [tolerance=±5% resistance=10k package="0805 [SMD]"]
  R11 = Resistor [tolerance=±5% resistance=10k package="0805 [SMD]"]
  X5 = RELAY-2 [package=relay-g5v]
  R12 = Resistor [tolerance=±5% resistance=10k package="0805 [SMD]"]
  Part1 = Arduino Uno (Rev3)

nets:
  12V: X1.2, D1.C, X2.2, D2.C, X3.2, D3.C
  N1: X1.9, D1.A, Q1.C
  GND: Q1.E, R2.Pin_0, Q2.E, R4.Pin_0, Q3.E, R6.Pin_0, X4.10, R7.Pin_1, R8.Pin_1, R9.Pin_1, R11.Pin_1, X5.10, Part1.GND
  N2: Q1.B, R1.Pin_1, R2.Pin_1
  oDoorUp: R1.Pin_0, Part1.D8
  N3: X2.9, D2.A, Q2.C
  N4: Q2.B, R3.Pin_1, R4.Pin_1
  oDoorEnable: R3.Pin_0, Part1.D10_PWM/SS
  N5: X3.9, D3.A, Q3.C
  N6: Q3.B, R5.Pin_1, R6.Pin_1
  oDoorDown: R5.Pin_0, Part1.D9_PWM
  iButtonUp: S1.leg0, R7.Pin_0, Part1.D4
  5V: S1.leg1, S2.leg1, S3.leg1, S5.leg1, R10.Pin_0, R12.Pin_0, Part1.5V
  iButtonStop: S2.leg0, R8.Pin_0, Part1.D5_PWM
  iButtonDown: S3.leg0, R9.Pin_0, Part1.D3_PWM
  iButtonRemote: X4.5, R10.Pin_1, Part1.D6_PWM
  iReedSwitch: S5.leg0, R11.Pin_0, Part1.D2
  iBreakBeam: X5.5, R12.Pin_1, Part1.D7

notes:
  Door-Down Control
  This portion emulates the down button being pressed, however also requires the 'enable' component to activate.
  Door-Enable Control
  This portion emulates any button being pressed. The Stop button on the existing system 'broke' this connection.
  Door-Up Control
  This portion emulates the up button being pressed, however also requires the 'enable' component to activate.
  Added remote control facility
  The existing Down-Button is wired to the micro controller to support existing operation.
  The existing Stop-Button is wired to the micro controller to support existing operation.
  The existing Up-Button is wired to the micro controller to support existing operation.
  The break beam allows the door to stop if something is obstructing it, or better yet, not begin traversing in the first place.<module fritzingVersion="0.9.2b.11.19.8d2d5970658f0bed09c661c9ea9a515b5f40f44c">
  <boundingRects>
  <boundingRect name="PCB View" rect="0 0 0 0"/>
  <boundingRect name="Breadboard View" rect="0 0 0 0"/>
  <boundingRect name="Schematic View" rect="-61.2256 -85.5045 43.2211 29.0045"/>
  </boundingRects>
  <instances>
  <instance path=":/resources/parts/core/netlabel.fzp" moduleIdRef="NetLabelModuleID" modelIndex="7803">
  <property value="oDoorEnable" name="label"/>
  <property value="right" name="direction"/>
  <title>oDoorEnable1</title>
  <views>
  <schematicView layer="schematic">
  <geometry z="2.50018" x="-61.2256" y="-76.5045"/>
  </schematicView>
  <breadboardView layer="schematic">
  <geometry z="2.50018" x="51.75" y="94.5"/>
  </breadboardView>
  <pcbView layer="schematic">
  <geometry z="2.50018" x="69.75" y="76.5"/>
  </pcbView>
  </views>
  </instance>
  <instance path=":/resources/parts/core/netlabel.fzp" moduleIdRef="NetLabelModuleID" modelIndex="7801">
  <property value="oDoorUp" name="label"/>
  <property value="right" name="direction"/>
  <title>oDoorUp1</title>
  <views>
  <schematicView layer="schematic">
  <geometry z="2.50018" x="-56.7648" y="-65.5"/>
  </schematicView>
  <breadboardView layer="schematic">
  <geometry z="2.50018" x="51.75" y="94.5"/>
  </breadboardView>
  <pcbView layer="schematic">
  <geometry z="2.50018" x="69.75" y="76.5"/>
  </pcbView>
  </views>
  </instance>
  <instance path=":/resources/parts/core/netlabel.fzp" moduleIdRef="NetLabelModuleID" modelIndex="7807">
  <property value="oDoorDown" name="label"/>
  <property value="right" name="direction"/>
  <title>oDoorDown2</title>
  <views>
  <schematicView layer="schematic">
  <geometry z="2.50018" x="-50.0772" y="-85.5045"/>
  </schematicView>
  <breadboardView layer="schematic">
  <geometry z="2.50018" x="51.75" y="94.5"/>
  </breadboardView>
  <pcbView layer="schematic">
  <geometry z="2.50018" x="69.75" y="76.5"/>
  </pcbView>
  </views>
  </instance>
  </instances>
  </module>
  This reed switch was part of an existing alarm system, and lets the uC know the door is all the way home.
